// Logisim project cpu.circ as structural Verilog
// CPU
module main (
  input  [31:0] RS_READ_VALUE,
  input  [31:0] RI_READ_VALUE,
  input  [31:0] RD_READ_VALUE,
  input  [31:0] JC_READ_VALUE,
  input  [31:0] INSTRUCTION,
  input  TEMP_JUMPENABLE,
  input  CLOCK,
  output [4:0] RS,
  output [4:0] RI,
  output [4:0] RD,
  output [31:0] RD_WRITE_VALUE,
  output RD_WRITE_ENABLE,
  output [23:0] FETCH_ADDRESS
);

  wire IMMEDIATEMUX, u_decode_1_immediateflag;
  wire [2:0] u_decode_1_jc;
  wire [3:0] OPCODE, u_decode_1_opcode;
  wire [4:0] u_decode_1_rd, u_decode_1_ri, u_decode_1_rs;
  wire [16:0] u_decode_1_imm;
  wire [23:0] u_decode_1_addr;
  wire [31:0] IMM, multiplexer_1_out;

  u_PC u_pc_1 (.JUMPENABLE(TEMP_JUMPENABLE), .CLOCK(CLOCK), .PC(FETCH_ADDRESS));  // open: JUMPADDR
  Multiplexer #(.width(32)) multiplexer_1 (
    .in0(IMM), .in1(RI_READ_VALUE), .out(multiplexer_1_out), .sel(IMMEDIATEMUX));  // open: en
  u_DECODE u_decode_1 (
    .INSTRUCTION(INSTRUCTION), .OPCODE(u_decode_1_opcode), .IMMEDIATEFLAG(u_decode_1_immediateflag),
    .RD(u_decode_1_rd), .RS(u_decode_1_rs), .RI(u_decode_1_ri), .IMM(u_decode_1_imm), .JC(u_decode_1_jc),
    .ADDR(u_decode_1_addr));
  u_CONTROL u_control_1 (
    .OPCODE(u_decode_1_opcode), .IMMEDIATEFLAG(u_decode_1_immediateflag), .RD(u_decode_1_rd),
    .RS(u_decode_1_rs), .RI(u_decode_1_ri), .IMM(u_decode_1_imm), .JC(u_decode_1_jc), .ADDR(u_decode_1_addr),
    .OPCODE_2(OPCODE), .IMMEDIATEMUX(IMMEDIATEMUX), .RD_2(RD), .RS_2(RS), .RI_2(RI), .IMM_2(IMM));
  u_ALU u_alu_1 (.ALU_X(RS_READ_VALUE), .ALU_Y(multiplexer_1_out), .ALU_CONTROL(OPCODE));  // open: ALU_RESULT
  u_MEM u_mem_1 ();  // open: ADDRESS, WORD_MODE, MEM_WRITE, DATA_IN, CLOCK, DATA_OUT

  // Other names for the same wires on the sheet: FETCHPC[23:0] = FETCH_ADDRESS

  // Notes on the sheet:
  //   This is here as a placeholder until we actually implement jump conditions
  //   Feel free to use these ALU/MEM components, or delete them!
endmodule

module u_ALU (
  input  [31:0] ALU_X,
  input  [31:0] ALU_Y,
  output [31:0] ALU_RESULT,
  output [3:0] ALU_CONTROL
);

  u_REV u_rev_1 ();  // open: INPUT, REVERSE_AMOUNT, OUTPUT
endmodule

// Data Memory
module u_MEM (
  input  [24:0] ADDRESS,
  input  WORD_MODE,
  input  MEM_WRITE,
  input  [31:0] DATA_IN,
  input  CLOCK,
  output [31:0] DATA_OUT
);


  // Notes on the sheet:
  //   Feel free to use this component, or not, however you want!
  //   You might use the word mode input to differentiate LW/SW from LH/SH.
  //   However, you *SHOULD* use 2 RAM modules, one for even addresses and one for odd addresses.
endmodule

module u_REV (
  input  [31:0] INPUT,
  input  [4:0] REVERSE_AMOUNT,
  output [31:0] OUTPUT
);


  // Notes on the sheet:
  //   Feel free to use this component, or not, however you want!
endmodule

module u_DECODE (
  input  [31:0] INSTRUCTION,
  output [3:0] OPCODE,
  output IMMEDIATEFLAG,
  output [4:0] RD,
  output [4:0] RS,
  output [4:0] RI,
  output [16:0] IMM,
  output [2:0] JC,
  output [23:0] ADDR
);


  assign ADDR = INSTRUCTION[23:0];
  assign IMM = INSTRUCTION[16:0];
  assign IMMEDIATEFLAG = INSTRUCTION[27];
  assign JC = INSTRUCTION[26:24];
  assign OPCODE = INSTRUCTION[31:28];
  assign RD = INSTRUCTION[26:22];
  assign RI = INSTRUCTION[4:0];
  assign RS = INSTRUCTION[21:17];

  // Other names for the same wires on the sheet: ADDRT[23:0] = INSTRUCTION[23:0];
  //   IMMEDIATET[16:0] = INSTRUCTION[16:0]; INSTRUCT[31:0] = INSTRUCTION; RIT[4:0] = INSTRUCTION[4:0];
  //   RST[4:0] = INSTRUCTION[21:17]; RDT[4:0] = INSTRUCTION[26:22]; JCT[2:0] = INSTRUCTION[26:24];
  //   IMMEDIATEFLAGT = INSTRUCTION[27]; OPCODET[3:0] = INSTRUCTION[31:28]
endmodule

module u_CONTROL (
  input  [3:0] OPCODE,
  input  IMMEDIATEFLAG,
  input  [4:0] RD,
  input  [4:0] RS,
  input  [4:0] RI,
  input  [16:0] IMM,
  input  [2:0] JC,
  input  [23:0] ADDR,
  output [3:0] OPCODE_2,
  output IMMEDIATEMUX,
  output [4:0] RD_2,
  output [4:0] RS_2,
  output [4:0] RI_2,
  output [31:0] IMM_2
);

  wire comparator_1_eq;
  wire [31:0] u_signextend17_1_immediate32;

  u_SIGNEXTEND17 u_signextend17_1 (.IMMEDIATE17(IMM), .IMMEDIATE32(u_signextend17_1_immediate32));
  Comparator #(.width(4), .mode("unsigned")) comparator_1 (
    .a(4'b1110), .b(OPCODE), .eq(comparator_1_eq));  // open: gt, lt
  Multiplexer #(.width(32)) multiplexer_1 (
    .in0(u_signextend17_1_immediate32), .in1({{15{1'b0}}, IMM}), .out(IMM_2), .sel(comparator_1_eq));  // open: en

  assign IMMEDIATEMUX = IMMEDIATEFLAG;
  assign OPCODE_2 = OPCODE;
  assign RD_2 = RD;
  assign RI_2 = RI;
  assign RS_2 = RS;

  // Notes on the sheet:
  //   Very Simple for now. Only considering R-Type instructions
  //   Do not sign extend for R-type instructions only for Set Upper Opcode=1110
endmodule

module u_PC (
  input  JUMPENABLE,
  input  [23:0] JUMPADDR,
  input  CLOCK,
  output [23:0] PC
);

  wire [23:0] multiplexer_1_out, NEXTPC;

  Multiplexer #(.width(24)) multiplexer_1 (
    .in0(NEXTPC), .in1(JUMPADDR), .out(multiplexer_1_out), .sel(JUMPENABLE));  // open: en
  Register #(.width(24)) u_PC (.D(multiplexer_1_out), .Q(PC), .clk(CLOCK));  // open: en, clr
  Adder #(.width(24)) adder_1 (.a(24'h1), .b(PC), .out(NEXTPC));  // open: cin, cout
endmodule

module u_SIGNEXTEND17 (
  input  [16:0] IMMEDIATE17,
  output [31:0] IMMEDIATE32
);

  assign IMMEDIATE32 = {{15{IMMEDIATE17[16]}}, IMMEDIATE17};  // Bit_Extender bit_extender_1
endmodule

module u_ALU_ADD (
  input  [31:0] ALU_X,
  input  [31:0] ALU_Y,
  output [31:0] RESULT
);

  Adder #(.width(32)) adder_1 (.a(ALU_X), .b(ALU_Y), .out(RESULT));  // open: cin, cout
endmodule

module u_ALU_SUB (
  input  [31:0] ALU_X,
  input  [31:0] ALU_Y,
  output [31:0] RESULT
);

  Subtractor #(.width(32)) subtractor_1 (.a(ALU_X), .b(ALU_Y), .out(RESULT));  // open: bin, bout
endmodule

module u_ALU_MUL (
  input  [31:0] ALU_X,
  input  [31:0] RESULT,
  input  [31:0] ALU_Y
);

  Multiplier #(.width(32)) multiplier_1 (.a(ALU_X), .b(ALU_Y), .out(RESULT));  // open: cin, cout
endmodule

module u_ALU_SL (
  input  [31:0] ALU_X,
  input  [31:0] ALU_Y,
  output [31:0] RESULT
);

  wire [31:0] CONT, CONT_2, multiplexer_1_out, multiplexer_2_out, u_alu_sl_shiftoneleft_1_result,
       u_alu_sl_shiftoneleft_2_result, u_alu_sl_shiftoneleft_3_result, u_alu_sl_shiftoneleft_4_result,
       u_alu_sl_shiftoneleft_5_result, u_alu_sl_shiftoneleft_6_result, u_alu_sl_shiftoneleft_7_result,
       u_alu_sl_shiftoneleft_8_result, u_alu_sl_shiftoneleft_9_result, u_alu_sl_shiftoneleft_10_result,
       u_alu_sl_shiftoneleft_11_result, u_alu_sl_shiftoneleft_12_result, u_alu_sl_shiftoneleft_13_result,
       u_alu_sl_shiftoneleft_14_result, u_alu_sl_shiftoneleft_15_result, u_alu_sl_shiftoneleft_16_result,
       u_alu_sl_shiftoneleft_17_result, u_alu_sl_shiftoneleft_18_result, u_alu_sl_shiftoneleft_19_result,
       u_alu_sl_shiftoneleft_20_result, u_alu_sl_shiftoneleft_21_result, u_alu_sl_shiftoneleft_22_result,
       u_alu_sl_shiftoneleft_23_result, u_alu_sl_shiftoneleft_24_result, u_alu_sl_shiftoneleft_25_result,
       u_alu_sl_shiftoneleft_26_result, u_alu_sl_shiftoneleft_27_result, u_alu_sl_shiftoneleft_28_result,
       u_alu_sl_shiftoneleft_29_result, u_alu_sl_shiftoneleft_30_result, u_alu_sl_shiftoneleft_31_result;

  u_ALU_SL_SHIFTONELEFT u_alu_sl_shiftoneleft_1 (
    .VALTOSHIFT(u_alu_sl_shiftoneleft_2_result), .RESULT(u_alu_sl_shiftoneleft_1_result));
  u_ALU_SL_SHIFTONELEFT u_alu_sl_shiftoneleft_2 (.VALTOSHIFT(CONT), .RESULT(u_alu_sl_shiftoneleft_2_result));
  u_ALU_SL_SHIFTONELEFT u_alu_sl_shiftoneleft_3 (.VALTOSHIFT(CONT_2), .RESULT(u_alu_sl_shiftoneleft_3_result));
  u_ALU_SL_SHIFTONELEFT u_alu_sl_shiftoneleft_4 (
    .VALTOSHIFT(u_alu_sl_shiftoneleft_3_result), .RESULT(u_alu_sl_shiftoneleft_4_result));
  u_ALU_SL_SHIFTONELEFT u_alu_sl_shiftoneleft_5 (.VALTOSHIFT(ALU_X), .RESULT(u_alu_sl_shiftoneleft_5_result));
  u_ALU_SL_SHIFTONELEFT u_alu_sl_shiftoneleft_6 (
    .VALTOSHIFT(u_alu_sl_shiftoneleft_1_result), .RESULT(u_alu_sl_shiftoneleft_6_result));
  u_ALU_SL_SHIFTONELEFT u_alu_sl_shiftoneleft_7 (
    .VALTOSHIFT(u_alu_sl_shiftoneleft_6_result), .RESULT(u_alu_sl_shiftoneleft_7_result));
  u_ALU_SL_SHIFTONELEFT u_alu_sl_shiftoneleft_8 (
    .VALTOSHIFT(u_alu_sl_shiftoneleft_4_result), .RESULT(u_alu_sl_shiftoneleft_8_result));
  u_ALU_SL_SHIFTONELEFT u_alu_sl_shiftoneleft_9 (
    .VALTOSHIFT(u_alu_sl_shiftoneleft_8_result), .RESULT(u_alu_sl_shiftoneleft_9_result));
  Multiplexer #(.width(32)) multiplexer_1 (
    .in0(ALU_X), .in1(u_alu_sl_shiftoneleft_5_result), .out(multiplexer_1_out), .sel(ALU_Y[0]));  // open: en
  u_ALU_SL_SHIFTONELEFT u_alu_sl_shiftoneleft_10 (
    .VALTOSHIFT(u_alu_sl_shiftoneleft_7_result), .RESULT(u_alu_sl_shiftoneleft_10_result));
  u_ALU_SL_SHIFTONELEFT u_alu_sl_shiftoneleft_11 (
    .VALTOSHIFT(u_alu_sl_shiftoneleft_10_result), .RESULT(u_alu_sl_shiftoneleft_11_result));
  u_ALU_SL_SHIFTONELEFT u_alu_sl_shiftoneleft_12 (
    .VALTOSHIFT(u_alu_sl_shiftoneleft_9_result), .RESULT(u_alu_sl_shiftoneleft_12_result));
  u_ALU_SL_SHIFTONELEFT u_alu_sl_shiftoneleft_13 (
    .VALTOSHIFT(u_alu_sl_shiftoneleft_12_result), .RESULT(u_alu_sl_shiftoneleft_13_result));
  u_ALU_SL_SHIFTONELEFT u_alu_sl_shiftoneleft_14 (
    .VALTOSHIFT(multiplexer_1_out), .RESULT(u_alu_sl_shiftoneleft_14_result));
  u_ALU_SL_SHIFTONELEFT u_alu_sl_shiftoneleft_15 (
    .VALTOSHIFT(u_alu_sl_shiftoneleft_11_result), .RESULT(u_alu_sl_shiftoneleft_15_result));
  u_ALU_SL_SHIFTONELEFT u_alu_sl_shiftoneleft_16 (
    .VALTOSHIFT(u_alu_sl_shiftoneleft_15_result), .RESULT(u_alu_sl_shiftoneleft_16_result));
  u_ALU_SL_SHIFTONELEFT u_alu_sl_shiftoneleft_17 (
    .VALTOSHIFT(u_alu_sl_shiftoneleft_18_result), .RESULT(u_alu_sl_shiftoneleft_17_result));
  u_ALU_SL_SHIFTONELEFT u_alu_sl_shiftoneleft_18 (
    .VALTOSHIFT(u_alu_sl_shiftoneleft_13_result), .RESULT(u_alu_sl_shiftoneleft_18_result));
  Multiplexer #(.width(32)) multiplexer_2 (
    .in0(multiplexer_1_out), .in1(u_alu_sl_shiftoneleft_19_result), .out(multiplexer_2_out), .sel(ALU_Y[1]));  // open: en
  u_ALU_SL_SHIFTONELEFT u_alu_sl_shiftoneleft_19 (
    .VALTOSHIFT(u_alu_sl_shiftoneleft_14_result), .RESULT(u_alu_sl_shiftoneleft_19_result));
  Multiplexer #(.width(32)) multiplexer_3 (
    .in0(CONT), .in1(u_alu_sl_shiftoneleft_16_result), .out(CONT_2), .sel(ALU_Y[3]));  // open: en
  u_ALU_SL_SHIFTONELEFT u_alu_sl_shiftoneleft_20 (
    .VALTOSHIFT(u_alu_sl_shiftoneleft_21_result), .RESULT(u_alu_sl_shiftoneleft_20_result));
  u_ALU_SL_SHIFTONELEFT u_alu_sl_shiftoneleft_21 (
    .VALTOSHIFT(u_alu_sl_shiftoneleft_17_result), .RESULT(u_alu_sl_shiftoneleft_21_result));
  u_ALU_SL_SHIFTONELEFT u_alu_sl_shiftoneleft_22 (
    .VALTOSHIFT(multiplexer_2_out), .RESULT(u_alu_sl_shiftoneleft_22_result));
  u_ALU_SL_SHIFTONELEFT u_alu_sl_shiftoneleft_23 (
    .VALTOSHIFT(u_alu_sl_shiftoneleft_24_result), .RESULT(u_alu_sl_shiftoneleft_23_result));
  u_ALU_SL_SHIFTONELEFT u_alu_sl_shiftoneleft_24 (
    .VALTOSHIFT(u_alu_sl_shiftoneleft_20_result), .RESULT(u_alu_sl_shiftoneleft_24_result));
  u_ALU_SL_SHIFTONELEFT u_alu_sl_shiftoneleft_25 (
    .VALTOSHIFT(u_alu_sl_shiftoneleft_22_result), .RESULT(u_alu_sl_shiftoneleft_25_result));
  u_ALU_SL_SHIFTONELEFT u_alu_sl_shiftoneleft_26 (
    .VALTOSHIFT(u_alu_sl_shiftoneleft_25_result), .RESULT(u_alu_sl_shiftoneleft_26_result));
  u_ALU_SL_SHIFTONELEFT u_alu_sl_shiftoneleft_27 (
    .VALTOSHIFT(u_alu_sl_shiftoneleft_28_result), .RESULT(u_alu_sl_shiftoneleft_27_result));
  u_ALU_SL_SHIFTONELEFT u_alu_sl_shiftoneleft_28 (
    .VALTOSHIFT(u_alu_sl_shiftoneleft_23_result), .RESULT(u_alu_sl_shiftoneleft_28_result));
  u_ALU_SL_SHIFTONELEFT u_alu_sl_shiftoneleft_29 (
    .VALTOSHIFT(u_alu_sl_shiftoneleft_26_result), .RESULT(u_alu_sl_shiftoneleft_29_result));
  u_ALU_SL_SHIFTONELEFT u_alu_sl_shiftoneleft_30 (
    .VALTOSHIFT(u_alu_sl_shiftoneleft_27_result), .RESULT(u_alu_sl_shiftoneleft_30_result));
  u_ALU_SL_SHIFTONELEFT u_alu_sl_shiftoneleft_31 (
    .VALTOSHIFT(u_alu_sl_shiftoneleft_30_result), .RESULT(u_alu_sl_shiftoneleft_31_result));
  Multiplexer #(.width(32)) multiplexer_4 (
    .in0(multiplexer_2_out), .in1(u_alu_sl_shiftoneleft_29_result), .out(CONT), .sel(ALU_Y[2]));  // open: en
  Multiplexer #(.width(32)) multiplexer_5 (
    .in0(CONT_2), .in1(u_alu_sl_shiftoneleft_31_result), .out(RESULT), .sel(ALU_Y[4]));  // open: en

  // Other names for the same wires on the sheet: SHIFT_1 = ALU_Y[0]; SHIFT_2 = ALU_Y[1]; SHIFT_4 = ALU_Y[2];
  //   SHIFT_8 = ALU_Y[3]; SHIFT_16 = ALU_Y[4]
endmodule

module u_ALU_SL_SHIFTONELEFT (
  input  [31:0] VALTOSHIFT,
  output [31:0] RESULT
);


  assign RESULT = {VALTOSHIFT[30:0], VALTOSHIFT[0]};
endmodule

module u_ALU_SR (
  input  [31:0] ALU_X,
  input  [31:0] ALU_Y,
  output [31:0] RESULT
);

  Shifter #(.width(32), .shift("ar")) shifter_1 (.in(ALU_X), .\dist (ALU_Y[4:0]), .out(RESULT));
endmodule

module u_ALU_AND (
  input  [31:0] ALU_X,
  input  [31:0] ALU_Y,
  output [31:0] RESULT
);

  assign RESULT = ALU_X & ALU_Y;  // AND_Gate and_1, 32 bits wide
endmodule

module u_ALU_OR (
  input  [31:0] ALU_X,
  input  [31:0] ALU_Y,
  output [31:0] RESULT
);

  assign RESULT = ALU_X | ALU_Y;  // OR_Gate or_1, 32 bits wide
endmodule

module u_ALU_XOR (
  input  [31:0] ALU_X,
  input  [31:0] ALU_Y,
  output [31:0] RESULT
);

  assign RESULT = ALU_X ^ ALU_Y;  // XOR_Gate xor_1, 32 bits wide
endmodule
